# Fritzing sketch Nano Motivator v1 (saved by Fritzing 1.0.5)
breadboards: 1

parts:
  DFRobot_DFPlayer_Mini1 = DFRobot DFPlayer Mini [part_number=DFR0299]
  SP1 = SPEAKER [package=pcb_mount_speaker]
  SP2 = SPEAKER [package=pcb_mount_speaker]
  J1 = Piezo Speaker
  C1 = Capacitor Polarized [package=cpol-radial-10uf-25v]
  Part2 = Adafruit Breadboard-Friendly NeoPixel [part_number="Adafruit #1312"]
  Part3 = Adafruit Breadboard-Friendly NeoPixel [part_number="Adafruit #1312"]
  U1 = 74AHCT125 [part_number=SN74AHCT125 package=dil14]
  A1 = Arduino Nano ESP32

nets:
  N1: DFRobot_DFPlayer_Mini1.VCC, C1.+, A1.Pin_15
  N2: DFRobot_DFPlayer_Mini1.RX, A1.Pin_21
  N3: DFRobot_DFPlayer_Mini1.TX, A1.Pin_20
  N4: DFRobot_DFPlayer_Mini1.DAC_R, SP1.-
  N5: DFRobot_DFPlayer_Mini1.DAC_L, SP2.-
  N6: DFRobot_DFPlayer_Mini1.SPK_1, J1.pin2
  N7: DFRobot_DFPlayer_Mini1.GND-1, DFRobot_DFPlayer_Mini1.GND-2, SP1.+, SP2.+, C1.-, A1.Pin_14, A1.Pin_19
  N8: DFRobot_DFPlayer_Mini1.SPK_2, J1.pin1
  N9: DFRobot_DFPlayer_Mini1.BUSY, A1.Pin_22
  N10: Part2.IN, U1.1OE
  N11: Part3.IN, U1.1A
  N12: U1.4OE, A1.Pin_25
  N13: U1.VCC, A1.Pin_24

notes:
  74AHCT125 other 3.3-5v Level Shifter
  D9 SBUS IN (UART Rx1)
  From FrSky receiver
  100µF electrolytic capacitor - VCC-GND to steady DFPlayer power
  Longer lead to VCC
  DAC is for unamplified output (AMP not shown here) or phono pin
  Amplified 3W mono speaker - NO GND
  Yellow: DF Rx to D3 (Tx Software Serial 9600 Baud)
  Green: DF Tx to D2 (Rx Software Serial 9600 Baud)
  Blue: Busy to D4
  WS2812b LEDs Data only shown
  D6 LED BANK (1)
  D7 LED BANK (2)

custom parts:
  Adafruit Breadboard-Friendly NeoPixel: This is the easiest way possible to add small, bright RGB pixels to your project. We took the same technology from our Flora NeoPixels and made them breadboard friendly, with two rows of 3 x 0.1" spaced header on each side for easy soldering, chaining and breadboarding. These ultra-bright LEDs have a constant-current driver cooked right into the LED package! The pixels are chainable - so you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
  74AHCT125: Quad Level-Shifter (3V to 5V) Quadruple Bus Buffer Gates With 3-State Outputs
  Arduino Nano ESP32: Arduino® Nano ESP32 tht.
