# Fritzing sketch Teensy Motivator v1 (saved by Fritzing 1.0.5)
breadboards: 3

parts:
  C1 = Capacitor Polarized [package=cpol-radial-10uf-25v]
  Part2 = Adafruit Breadboard-Friendly NeoPixel [part_number="Adafruit #1312"]
  Part3 = Adafruit Breadboard-Friendly NeoPixel [part_number="Adafruit #1312"]
  DFRobot_DFPlayer_Mini2 = DFRobot DFPlayer Mini [part_number=DFR0299]
  J2 = Piezo Speaker
  SP3 = SPEAKER [package=pcb_mount_speaker]
  SP4 = SPEAKER [package=pcb_mount_speaker]
  A1 = Teensy 4.1
  Adafruit_Mini_Sparkle_Motion1 = Adafruit Mini Sparkle Motion [part_number=#6160]

nets:
  N1: C1.+, DFRobot_DFPlayer_Mini2.VCC, A1.Pin_64
  N2: C1.-, DFRobot_DFPlayer_Mini2.GND-1, DFRobot_DFPlayer_Mini2.GND-2, A1.Pin_11, A1.Pin_12, A1.Pin_38, A1.Pin_50, A1.Pin_63
  N3: Part2.IN, Adafruit_Mini_Sparkle_Motion1.S1
  N4: Part3.IN, Adafruit_Mini_Sparkle_Motion1.S2
  N5: DFRobot_DFPlayer_Mini2.RX, A1.Pin_21
  N6: DFRobot_DFPlayer_Mini2.TX, A1.Pin_20
  N7: DFRobot_DFPlayer_Mini2.DAC_R, SP3.-
  N8: DFRobot_DFPlayer_Mini2.DAC_L, SP4.-
  N9: DFRobot_DFPlayer_Mini2.SPK_1, J2.pin1
  N10: DFRobot_DFPlayer_Mini2.SPK_2, J2.pin2
  N11: DFRobot_DFPlayer_Mini2.BUSY, A1.Pin_19
  N12: SP3.+, SP4.+
  N13: A1.Pin_26, A1.Pin_62
  N14: A1.Pin_58, Adafruit_Mini_Sparkle_Motion1.IO25
  N15: A1.Pin_59, Adafruit_Mini_Sparkle_Motion1.IO26

notes:
  Yellow: TPin 28 (Rx7) to Maestro Tx
  Orange: TPin 29 (Tx7) to Maestro Rx
  White: TPin 34 (RX8) SBUS IN
  100µF electrolytic capacitor - VCC-GND to steady DFPlayer power
  Longer lead to VCC
  DAC is for unamplified output (AMP not shown here) or phono pin
  Amplified 3W mono speaker - NO GND
  Green: TPin 21 (RX5) to Sparkle Tx Pin 25
  Yellow: TPin 20 (TX5) to Sparkle Rx Pin 26
  WS2812b LEDs Data only shown
  D6 LED BANK (1)
  D7 LED BANK (2)
  VIN, GND, 3.3v
  Blue: TPin 6 to DF Busy
  Green: TPin 7 (RX2) to DF TX
  Yellow: TPin 8 (TX2) to DF RX
  Ochre: TPin 30 CRX3 Can Bus
  Purple: TPin 31 CTX3 Can Bus
  White: TPin 19 (SCL) for I2C
  Orange: TPin 18 (SDA) for I2C

custom parts:
  Adafruit Breadboard-Friendly NeoPixel: This is the easiest way possible to add small, bright RGB pixels to your project. We took the same technology from our Flora NeoPixels and made them breadboard friendly, with two rows of 3 x 0.1" spaced header on each side for easy soldering, chaining and breadboarding. These ultra-bright LEDs have a constant-current driver cooked right into the LED package! The pixels are chainable - so you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
  Teensy 4.1: The Teensy is a complete USB-based microcontoller development system, in a very small footprint, capable of implementing many types of projects. All programming is done via the USB port. No special programmer is needed, only a standard micro-USB cable and a PC or Macintosh with a USB port.
  Adafruit Mini Sparkle Motion: The Adafruit Sparkle Motion Mini is part of our series of "Sparkle Motion" boards, that are our attempt to make the best small WLED-friendly smart LED driving board in the whole world. Our resident mermaid, firepixie makes a lot of projects with WLED and she loves it! So how can we make something that will be powerful enough to drive advanced LED projects that need a compact design? The Mini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
